// Logisim project crc_8bits.circ as structural Verilog: 5 circuits, main circuit erro
module erro (
  input  c0,
  input  c1,
  input  c2,
  input  c3,
  input  c4,
  input  c5,
  input  c6,
  input  c7,
  input  n0,
  input  n1,
  input  n2,
  input  n3,
  input  n4,
  input  n5,
  input  n6,
  input  n7,
  input  n8,
  output erro
);

  wire and_1_out, or_1_out, or_2_out, or_3_out;

  or or_1 (or_1_out, c0, c1, c2, c3);
  or or_2 (or_2_out, c4, c5, c6, c7);
  or or_3 (or_3_out, or_1_out, or_2_out);
  and and_1 (and_1_out, ~n0, ~n1, n2, n3, n4, n5, n6, n7, n8);  // AND_Gate
  and and_2 (erro, or_3_out, and_1_out);
endmodule

module comp_op (
  input  Cn,
  input  Dado,
  input  clk,
  input  Pn,
  input  rst,
  output cn1
);

  wire and_1_out, and_2_out, or_1_out, xor_1_out;

  and and_1 (and_1_out, ~Cn, Dado);  // AND_Gate
  xor xor_1 (xor_1_out, Dado, Pn);
  and and_2 (and_2_out, Cn, xor_1_out);
  or or_1 (or_1_out, and_1_out, and_2_out);
  D_Flip_Flop d_ff_1 (.D(or_1_out), .clk(clk), .Q(cn1), .reset(rst));  // open: Qn, preset
endmodule

module n508 (
  input  c0,
  input  c1,
  input  c2,
  input  c3,
  input  c4,
  input  c5,
  input  c6,
  input  c7,
  input  c8,
  output stop
);

  wire and_1_out;

  and and_1 (and_1_out, ~c0, ~c1, c2, c3, c4, c5, c6, c7, c8);  // AND_Gate
  not not_1 (stop, and_1_out);
endmodule

module cont508 (
  input  strt,
  input  rst,
  output clk,
  output [8:0] cont
);

  wire clock_1_out, nao508;

  and and_1 (clk, strt, clock_1_out, nao508);
  Clock clock_1 (.out(clock_1_out));
  Counter #(.width(9), .max('h1ff)) counter_1 (.clr(rst), .clk(clk), .Q(cont));  // open: load, up, count, D, carry
  n508 n508_1 (
    .c0(cont[0]), .c1(cont[1]), .c2(cont[2]), .c3(cont[3]), .c4(cont[4]), .c5(cont[5]), .c6(cont[6]),
    .c7(cont[7]), .c8(cont[8]), .stop(nao508));

  // Other names for the same wires on the sheet: reset = rst; start = strt
endmodule

module crc8bits (
  input  start,
  input  reset,
  input  [8:0] in_3,
  output error
);

  wire comp_op_1_cn1, cont508_1_clk, sc0, sc1, sc2, sc3, sc4, sc5, sc6, sc7, undriven;
  wire [8:0] cont;

  ROM #(.addrWidth(9), .dataWidth(1)) rom_1 (.addr(cont));  // open: data
  cont508 cont508_1 (.strt(start), .rst(reset), .clk(cont508_1_clk), .cont(cont));
  comp_op c0 (.rst(reset), .Pn(in_3[0]), .clk(cont508_1_clk), .Dado(undriven), .Cn(sc7), .cn1(sc0));
  comp_op c1 (.rst(reset), .Pn(in_3[1]), .clk(cont508_1_clk), .Dado(sc0), .Cn(sc7), .cn1(sc1));
  comp_op c2 (.rst(reset), .Pn(in_3[2]), .clk(cont508_1_clk), .Dado(sc1), .Cn(sc7), .cn1(sc2));
  comp_op c3 (.rst(reset), .Pn(in_3[3]), .clk(cont508_1_clk), .Dado(sc2), .Cn(sc7), .cn1(sc3));
  comp_op c4 (.rst(reset), .Pn(in_3[4]), .clk(cont508_1_clk), .Dado(sc3), .Cn(sc7), .cn1(sc4));
  comp_op c5 (.rst(reset), .Pn(in_3[5]), .clk(cont508_1_clk), .Dado(sc4), .Cn(sc7), .cn1(sc5));
  comp_op c6 (.rst(reset), .Pn(in_3[6]), .clk(cont508_1_clk), .Dado(sc5), .Cn(sc7), .cn1(sc6));
  comp_op c7 (.rst(reset), .Pn(in_3[7]), .clk(cont508_1_clk), .Dado(sc6), .Cn(sc7), .cn1(sc7));
  erro erro_1 (
    .c0(sc0), .c1(sc1), .c2(sc2), .c3(sc3), .c4(sc4), .c5(sc5), .c6(sc6), .c7(sc7), .n0(cont[0]),
    .n1(cont[1]), .n2(cont[2]), .n3(cont[3]), .n4(cont[4]), .n5(cont[5]), .n6(cont[6]), .n7(cont[7]),
    .n8(cont[8]), .erro(error));
  comp_op comp_op_1 (.rst(reset), .Pn(in_3[8]), .clk(cont508_1_clk), .Dado(sc7), .Cn(sc7), .cn1(comp_op_1_cn1));

  // Notes on the sheet:
  //   in_3: pull=down
  //   contents of rom_1 (hex, n*v repeats v):
  //   1 1 0 1 0 4*1 0 1 1 0 0 1 1 0 0 5*1 0 1 0 0 0 1 0 7*1 0 1 1 1 0 1 1 0 0 0 1 6*0 1 1 0 1 0 1 0 1 0 0
  //   1 0 1 0 1 0 4*1 0 1 1 0 0 1 0 1 0 1 7*0 1 1 0 0 0 1 1 0 0 0 1 0 1 1 0 0 1 1 1 0 1 7*0 1 1 1 0 1 0 0
  //   1 1 1 0 5*1 0 1 1 1 0 0 1 0 0 1 1 0 1 0 0 1 1 1 0 0 1 0 0 0 1 0 0 0 1 0 1 0 0 1 1 1 0 0 0 5*1 0 0 1
  //   1 1 0 1 4*0 1 1 5*0 4*1 0 0 0 1 0 0 0 1 0 0 1 0 0 0 1 6*0 1 1 0 0 1 0 1 0 0 1 1 0 0 0 5*1 0 1 0 1 1
  //   0 0 1 1 7*0 1 0 1 1 0 0 0 7*1 0 0 0 1 1 0 4*1 7*0 4*1 0 1 0 0 5*1 0 1 0 1 0 1 0 1 6*0 1 1 0 5*1 0 1
  //   1 0 0 1 0 1 1 0 0 1 0 0 6*1 4*0 1 0 1 0 1 0 1 0 0 0 1 0 0 1 0 1 1 0 1 0 0 0 1 0 0 1 0 1 0 1 0 0 1 1
  //   0 1 0 1 0 0 1 0 1 0 1 1 1 0 0 1 1 1 0 1 0 0 1 1 0 0 0 1 0 0 1 0 1 1 0 0 1 0 1 1 0 0 1 1 1 0 0 1 4*0
  //   1 8*0 1 0 1 0 0 1 4*0 1 5*0 1 4*0 1 1 0 0 1 1 0 1 5*0 1 1 0 0 1 0 1 1 0 1 1 0 1 0 1 0 0 1 0 0 1 0 1
  //   0 0 4*1 0 1
endmodule
