// Logisim project gerador_de_mensagens.circ as structural Verilog: 2 circuits, main circuit main
module main (
  input  start,
  input  reset
);

  wire and_1_out, clock_1_out, controlled_buffer_1_out, nao500, random_1_out;
  wire [9:0] counter_1_q;

  Clock clock_1 (.out(clock_1_out));
  and and_1 (and_1_out, start, nao500);
  assign controlled_buffer_1_out = and_1_out ? clock_1_out : 1'bz;  // Controlled_Buffer controlled_buffer_1
  Counter #(.width(10), .max('h3ff)) counter_1 (
    .clr(reset), .clk(controlled_buffer_1_out), .Q(counter_1_q));  // open: load, up, count, D, carry
  n500 n500_1 (
    .c0(counter_1_q[0]), .c1(counter_1_q[1]), .c2(counter_1_q[2]), .c3(counter_1_q[3]), .c4(counter_1_q[4]),
    .c5(counter_1_q[5]), .c6(counter_1_q[6]), .c7(counter_1_q[7]), .c8(counter_1_q[8]), .stop(nao500));
  Random #(.width(1)) random_1 (.clr(reset), .clk(controlled_buffer_1_out), .out(random_1_out));  // open: next
  RAM #(.addrWidth(10), .dataWidth(1), .databus("bibus")) ram_1 (
    .addr(counter_1_q), .we(start), .clk(controlled_buffer_1_out), .din(random_1_out));  // open: oe, dout
endmodule

module n500 (
  input  c0,
  input  c1,
  input  c2,
  input  c3,
  input  c4,
  input  c5,
  input  c6,
  input  c7,
  input  c8,
  output stop
);

  wire and_1_out;

  and and_1 (and_1_out, ~c0, ~c1, c2, ~c3, c4, c5, c6, c7, c8);  // AND_Gate
  not not_1 (stop, and_1_out);
endmodule
